// Logisim project Digital_Project_Elevator.circ as structural Verilog: 11 circuits, main circuit in_car_bc9929b8
module in_car_bc9929b8 (
);

  wire APP1_out, APP2_out, APP3_out, APP4_out, button_1_out, button_2_out, button_6_out, button_7_out,
       button_8_out, button_9_out, button_latches_ae447a43_1_at_stop_46b7d8da,
       button_latches_ae447a43_1_call_above_715101cc, button_latches_ae447a43_1_call_active_715e6a8a,
       button_latches_ae447a43_1_call_below_fc8ecee0, direction_decode_e6330b5d_1_direction,
       door_sim_7d0fcb8b_1_door_status_af08e2fd, floor_appproach_58257a26_1_approach, L_2_28af8a88_out,
       L_3_dd358ec4_out, motor_door_logic_fa23df24_1_cmd_door_open_19b56e78,
       motor_door_logic_fa23df24_1_cmd_slow_en_6e5f7d0c, motor_door_logic_fa23df24_1_door_done_547bfa6b,
       motor_door_logic_fa23df24_1_motor_dn_6e157126, motor_door_logic_fa23df24_1_motor_up_ea3cc64a,
       RESET_out;
  wire [3:0] button_3_out, floor_appproach_58257a26_1_p1l;

  Button button_1 (.out(button_1_out));
  Button L_3_dd358ec4 (.out(L_3_dd358ec4_out));
  Button L_2_28af8a88 (.out(L_2_28af8a88_out));
  Button button_2 (.out(button_2_out));
  Button button_3 (.out(button_3_out[0]));
  Button button_4 (.out(button_3_out[1]));
  Button button_5 (.out(button_3_out[2]));
  Button L_1_e18e0e2f (.out(button_3_out[3]));
  Button RESET (.out(RESET_out));
  Button APP4 (.out(APP4_out));
  Button APP3 (.out(APP3_out));
  Button APP2 (.out(APP2_out));
  Button APP1 (.out(APP1_out));
  Button button_6 (.out(button_6_out));
  Button button_7 (.out(button_7_out));
  Button button_8 (.out(button_8_out));
  Button button_9 (.out(button_9_out));
  BUTTON_LATCHES_ae447a43 button_latches_ae447a43_1 (
    .AT_STOP_46b7d8da(button_latches_ae447a43_1_at_stop_46b7d8da),
    .CALL_ACTIVE_715e6a8a(button_latches_ae447a43_1_call_active_715e6a8a),
    .CALL_ABOVE_715101cc(button_latches_ae447a43_1_call_above_715101cc),
    .CALL_BELOW_fc8ecee0(button_latches_ae447a43_1_call_below_fc8ecee0), .CALL_1_d5b07b17(button_2_out),
    .SEL_1_e9639fb3(button_3_out[3]), .POS_1_63d6ef2b(floor_appproach_58257a26_1_p1l[0]),
    .CALL_2_5f0a59fb(L_2_28af8a88_out), .SEL_2_1d3c80f6(button_3_out[2]),
    .POS_2_66b3fa52(floor_appproach_58257a26_1_p1l[1]), .CALL_3_4462af2b(L_3_dd358ec4_out),
    .SEL_3_6d29e9f3(button_3_out[1]), .POS_3_0e2c95fa(floor_appproach_58257a26_1_p1l[2]),
    .CALL_4_92d7caa6(button_1_out), .SEL_4_73dcaca7(button_3_out[0]),
    .POS_4_90082566(floor_appproach_58257a26_1_p1l[3]),
    .DOOR_DONE_547bfa6b(motor_door_logic_fa23df24_1_door_done_547bfa6b), .RESET(RESET_out));
  FLOOR_APPPROACH_58257a26 floor_appproach_58257a26_1 (
    .P2L(floor_appproach_58257a26_1_p1l[1]), .P3L(floor_appproach_58257a26_1_p1l[2]),
    .P4L(floor_appproach_58257a26_1_p1l[3]), .P1L(floor_appproach_58257a26_1_p1l[0]),
    .APPROACH(floor_appproach_58257a26_1_approach), .P1(button_8_out), .P2(button_9_out), .P3(button_6_out),
    .P4(button_7_out), .APP4(APP4_out), .APP3(APP3_out), .APP2(APP2_out), .APP1(APP1_out));
  LED CALL_ACTIVE_715e6a8a (.in(button_latches_ae447a43_1_call_active_715e6a8a));
  LED APPROACH (.in(floor_appproach_58257a26_1_approach));
  LED L_4_8e70c037 (.in(floor_appproach_58257a26_1_p1l[3]));
  LED led_1 (.in(floor_appproach_58257a26_1_p1l[2]));
  LED led_2 (.in(floor_appproach_58257a26_1_p1l[1]));
  LED led_3 (.in(floor_appproach_58257a26_1_p1l[0]));
  DIRECTION_DECODE_e6330b5d direction_decode_e6330b5d_1 (
    .DIRECTION(direction_decode_e6330b5d_1_direction),
    .DOWN_CALL_4aac5db2(button_latches_ae447a43_1_call_below_fc8ecee0),
    .UP_CALL_39970cbc(button_latches_ae447a43_1_call_above_715101cc));
  LED AT_STOP_46b7d8da (.in(button_latches_ae447a43_1_at_stop_46b7d8da));
  LED DIRECTION (.in(direction_decode_e6330b5d_1_direction));
  MOTOR_DOOR_LOGIC_fa23df24 motor_door_logic_fa23df24_1 (
    .MOTOR_UP_ea3cc64a(motor_door_logic_fa23df24_1_motor_up_ea3cc64a),
    .MOTOR_DN_6e157126(motor_door_logic_fa23df24_1_motor_dn_6e157126),
    .CMD_SLOW_EN_6e5f7d0c(motor_door_logic_fa23df24_1_cmd_slow_en_6e5f7d0c),
    .CMD_DOOR_OPEN_19b56e78(motor_door_logic_fa23df24_1_cmd_door_open_19b56e78),
    .DOOR_DONE_547bfa6b(motor_door_logic_fa23df24_1_door_done_547bfa6b),
    .CALL_ACTIVE_715e6a8a(button_latches_ae447a43_1_call_active_715e6a8a),
    .APPROACH(floor_appproach_58257a26_1_approach),
    .AT_STOP_46b7d8da(button_latches_ae447a43_1_at_stop_46b7d8da),
    .DOOR_STATUS_af08e2fd(door_sim_7d0fcb8b_1_door_status_af08e2fd),
    .DIRECTION(direction_decode_e6330b5d_1_direction));
  DOOR_SIM_7d0fcb8b door_sim_7d0fcb8b_1 (
    .DOOR_STATUS_af08e2fd(door_sim_7d0fcb8b_1_door_status_af08e2fd),
    .CMD_OPEN_629398b5(motor_door_logic_fa23df24_1_cmd_door_open_19b56e78));
  LED MOTOR_UP_48e201b7 (.in(motor_door_logic_fa23df24_1_motor_up_ea3cc64a));
  LED MOTOR_DN_f43bb3b6 (.in(motor_door_logic_fa23df24_1_motor_dn_6e157126));
  LED CMD_SLOW_9b005498 (.in(motor_door_logic_fa23df24_1_cmd_slow_en_6e5f7d0c));
  LED CMD_OPEN_629398b5 (.in(motor_door_logic_fa23df24_1_cmd_door_open_19b56e78));
  LED DOOR_OPEN_df92fb24 (.in(door_sim_7d0fcb8b_1_door_status_af08e2fd));
  LED DOOR_DONE_547bfa6b (.in(motor_door_logic_fa23df24_1_door_done_547bfa6b));

  // Notes on the sheet:
  //   FLOOR CALL
  //   BUTTONS
  //   SELECT
  //   BUTTONS
  //   FLOOR
  //   APPROACH
  //   SWITCHES
  //   WIRED IN SERIES
  //   ELEVATOR POSIITION
  //   CLEAR SELECTED FLOOR  MEMORY
  //   ELEVATOR POSITION
  //   APPROACHING FLOOR
  //   ON=UP
endmodule

module NOR_LATCH_2a7b4e3e (
  input  S,
  input  R,
  output Q
);

  wire clock_1_out, clock_2_out, j_k_ff_1_q, j_k_ff_1_qn, not_1_out, undriven, undriven_2;

  Clock clock_1 (.out(clock_1_out));
  S_R_Flip_Flop s_r_ff_1 (.R(1'b0), .clk(1'b0), .reset(1'b1), .preset(Q));  // open: S, Q, Qn
  Clock #(.highDuration(20), .lowDuration(20)) clock_2 (.out(clock_2_out));
  not not_1 (not_1_out, clock_2_out);
  J_K_Flip_Flop j_k_ff_1 (
    .J(undriven), .clk(not_1_out), .K(undriven_2), .Q(j_k_ff_1_q), .Qn(j_k_ff_1_qn), .preset(1'b0),
    .reset(1'b0));

  // Notes on the sheet:
  //   J
  //   K
  //   LM555
  //   J K FLIP FLOP
  //   PRE
  //   CLR
  //   EN
  //   NOT PART OF CIRCUIT
  //   Q
  //   Q'
endmodule

module FLOOR_APPPROACH_58257a26 (
  input  P1,
  input  APP4,
  input  P2,
  input  APP3,
  input  P3,
  input  APP2,
  input  P4,
  input  APP1,
  output P1L,
  output P2L,
  output APPROACH,
  output P3L,
  output P4L
);

  wire or_1_out, or_2_out, or_3_out, or_4_out;

  or or_1 (or_1_out, P2, P3, P4);
  or or_2 (or_2_out, P1, P3, P4);
  or or_3 (or_3_out, P1, P2, P4);
  or or_4 (or_4_out, P1, P2, P3);
  NOR_LATCH_2a7b4e3e nor_latch_2a7b4e3e_1 (.Q(P1L), .R(or_1_out), .S(P1));
  NOR_LATCH_2a7b4e3e nor_latch_2a7b4e3e_2 (.Q(P2L), .R(or_2_out), .S(P2));
  NOR_LATCH_2a7b4e3e nor_latch_2a7b4e3e_3 (.Q(P3L), .R(or_3_out), .S(P3));
  NOR_LATCH_2a7b4e3e nor_latch_2a7b4e3e_4 (.Q(P4L), .R(or_4_out), .S(P4));
  or or_5 (APPROACH, APP4, APP3, APP2, APP1);

  // Notes on the sheet:
  //   PULSE
endmodule

module L_4_16_DECODE_d250a9dc (
);

  wire clock_1_out, d_ff_1_q, d_ff_2_q, d_ff_3_q, d_ff_4_q, or_1_out, or_2_out, or_3_out, or_4_out;
  wire [2:0] undriven_2;
  wire [3:0] undriven;

  Decoder #(.enable("false"), .select(4)) decoder_1 (.sel(undriven));  // open: out0, out1, out2, out3, out4, out5, out6, out7, out8, out9, out10, out11, out12, out13, out14, out15
  Decoder #(.enable("false"), .select(3)) decoder_2 (.sel(undriven_2));  // open: out0, out1, out2, out3, out4, out5, out6, out7
  Clock clock_1 (.out(clock_1_out));
  // OR_Gate or_1 has open pins: out=or_1_out
  // OR_Gate or_2 has open pins: out=or_2_out
  // OR_Gate or_3 has open pins: out=or_3_out
  // OR_Gate or_4 has open pins: out=or_4_out
  D_Flip_Flop d_ff_1 (.clk(clock_1_out), .D(or_1_out), .Q(d_ff_1_q), .preset(1'b0), .reset(1'b0));  // open: Qn
  D_Flip_Flop d_ff_2 (.clk(clock_1_out), .D(or_2_out), .Q(d_ff_2_q), .preset(1'b0), .reset(1'b0));  // open: Qn
  D_Flip_Flop d_ff_3 (.clk(clock_1_out), .D(or_3_out), .Q(d_ff_3_q), .preset(1'b0), .reset(1'b0));  // open: Qn
  D_Flip_Flop d_ff_4 (.clk(clock_1_out), .D(or_4_out), .Q(d_ff_4_q), .preset(1'b0), .reset(1'b0));  // open: Qn

  // Notes on the sheet:
  //   IN
  //   CLR
  //   PRE
  //   EN
  //   CLR
  //   PRE
  //   EN
  //   CLR
  //   PRE
  //   EN
  //   CLR
  //   PRE
  //   EN
endmodule

module TEST (
  input  A,
  input  B,
  input  C,
  input  SHIFT,
  input  DATA_BITS_OUT,
  output out_6
);

  wire and_1_out, and_2_out, and_3_out, and_4_out, button_1_out, clock_1_out, clock_2_out, d_ff_1_q,
       not_1_out, not_2_out, not_3_out, not_4_out, shift_register_1_p1, shift_register_1_p8,
       shift_register_1_p9, shift_register_1_p10;

  not not_1 (not_1_out, A);
  not not_2 (not_2_out, B);
  not not_3 (not_3_out, C);
  not not_4 (not_4_out, SHIFT);
  Clock #(.highDuration(10), .lowDuration(10)) clock_1 (.out(clock_1_out));
  // Shift_Register #(.length(4)) shift_register_1: pin names not known; wires that end beside it: shift_register_1_p1, not_4_out, shift_register_1_p1, clock_1_out, SHIFT, DATA_BITS_OUT, 1'b1, shift_register_1_p8, shift_register_1_p9, shift_register_1_p10
  and and_1 (and_1_out, not_1_out, not_2_out);
  and and_2 (and_2_out, not_2_out, C);
  and and_3 (and_3_out, not_1_out, C);
  and and_4 (and_4_out, A, B, not_3_out);
  or or_1 (out_6, and_1_out, and_2_out, and_3_out, and_4_out);
  LED led_1 (.in(shift_register_1_p10));
  LED led_2 (.in(shift_register_1_p9));
  LED led_3 (.in(shift_register_1_p8));
  Clock #(.highDuration(10), .lowDuration(10)) clock_2 (.out(clock_2_out));
  Button button_1 (.out(button_1_out));
  D_Flip_Flop d_ff_1 (.clk(clock_2_out), .D(button_1_out), .Q(d_ff_1_q), .preset(1'b0), .reset(1'b0));  // open: Qn

  // Notes on the sheet:
  //   DATA
  //   LD
  //   CLK
  //   CLR
  //   1
  //   2
  //   3
  //   4
  //   4 BIT SHIFT REG.
  //   DATA BITS IN
  //   OUTPUT
  //   CLOSED
  //   OPEN
  //   D FLIP FLOP
  //   D
  //   SET
  //   RES
  //   EN
endmodule

module MOTOR_DOOR_LOGIC_fa23df24 (
  input  DIRECTION,
  input  CALL_ACTIVE_715e6a8a,
  input  APPROACH,
  input  AT_STOP_46b7d8da,
  input  DOOR_STATUS_af08e2fd,
  output MOTOR_UP_ea3cc64a,
  output MOTOR_DN_6e157126,
  output CMD_SLOW_EN_6e5f7d0c,
  output CMD_DOOR_OPEN_19b56e78,
  output DOOR_DONE_547bfa6b
);

  wire and_1_out, and_2_out, nor_latch_2a7b4e3e_2_q, not_1_out, not_2_out, not_3_out, not_4_out, not_5_out,
       not_6_out;

  not not_1 (not_1_out, AT_STOP_46b7d8da);
  not not_2 (not_2_out, DOOR_STATUS_af08e2fd);
  and and_1 (and_1_out, CALL_ACTIVE_715e6a8a, not_1_out, not_2_out);
  not not_3 (not_3_out, AT_STOP_46b7d8da);
  and and_2 (and_2_out, AT_STOP_46b7d8da, DOOR_STATUS_af08e2fd);
  not not_4 (not_4_out, DIRECTION);
  NOR_LATCH_2a7b4e3e nor_latch_2a7b4e3e_1 (.Q(CMD_SLOW_EN_6e5f7d0c), .R(AT_STOP_46b7d8da), .S(APPROACH));
  not not_5 (not_5_out, DOOR_STATUS_af08e2fd);
  not not_6 (not_6_out, nor_latch_2a7b4e3e_2_q);
  NOR_LATCH_2a7b4e3e nor_latch_2a7b4e3e_2 (.Q(nor_latch_2a7b4e3e_2_q), .R(not_3_out), .S(and_2_out));
  and and_3 (MOTOR_UP_ea3cc64a, DIRECTION, and_1_out);
  and and_4 (MOTOR_DN_6e157126, not_4_out, and_1_out);
  and and_5 (CMD_DOOR_OPEN_19b56e78, AT_STOP_46b7d8da, not_5_out, not_6_out);
  and and_6 (DOOR_DONE_547bfa6b, AT_STOP_46b7d8da, not_5_out, nor_latch_2a7b4e3e_2_q);

  // Notes on the sheet:
  //   1=UP
  //   PULSE
  //   NO STOPS
  //   0=CLOSED
  //   DOOR CLOSED
  //   MOTOR EN
  //   RESET IF NOT AT STOP
  //   ALLOWS MOVEMENT IF OTHER CALLS EXIST
  //   CLEARS CALL LATCH AT CURRENT FLOOR
endmodule

module BUTTON_LATCHES_ae447a43 (
  input  CALL_1_d5b07b17,
  input  SEL_1_e9639fb3,
  input  POS_1_63d6ef2b,
  input  CALL_2_5f0a59fb,
  input  SEL_2_1d3c80f6,
  input  POS_2_66b3fa52,
  input  CALL_3_4462af2b,
  input  SEL_3_6d29e9f3,
  input  POS_3_0e2c95fa,
  input  CALL_4_92d7caa6,
  input  SEL_4_73dcaca7,
  input  POS_4_90082566,
  input  DOOR_DONE_547bfa6b,
  input  RESET,
  output AT_STOP_46b7d8da,
  output CALL_ACTIVE_715e6a8a,
  output CALL_ABOVE_715101cc,
  output CALL_BELOW_fc8ecee0
);

  wire and_1_out, and_2_out, and_3_out, and_4_out, and_5_out, and_6_out, and_7_out, and_8_out, and_9_out,
       and_10_out, and_11_out, and_12_out, and_13_out, and_14_out, nor_latch_2a7b4e3e_1_q,
       nor_latch_2a7b4e3e_2_q, nor_latch_2a7b4e3e_3_q, nor_latch_2a7b4e3e_4_q, or_1_out, or_2_out, or_3_out,
       or_4_out, or_5_out, or_6_out, or_7_out, or_8_out, or_10_out, or_11_out, or_12_out, or_13_out;

  or or_1 (or_1_out, CALL_1_d5b07b17, SEL_1_e9639fb3);
  and and_1 (and_1_out, POS_1_63d6ef2b, DOOR_DONE_547bfa6b);
  or or_2 (or_2_out, and_1_out, RESET);
  or or_3 (or_3_out, CALL_2_5f0a59fb, SEL_2_1d3c80f6);
  and and_2 (and_2_out, POS_2_66b3fa52, DOOR_DONE_547bfa6b);
  or or_4 (or_4_out, and_2_out, RESET);
  or or_5 (or_5_out, CALL_3_4462af2b, SEL_3_6d29e9f3);
  and and_3 (and_3_out, POS_3_0e2c95fa, DOOR_DONE_547bfa6b);
  or or_6 (or_6_out, and_3_out, RESET);
  or or_7 (or_7_out, CALL_4_92d7caa6, SEL_4_73dcaca7);
  and and_4 (and_4_out, POS_4_90082566, DOOR_DONE_547bfa6b);
  or or_8 (or_8_out, and_4_out, RESET);
  NOR_LATCH_2a7b4e3e nor_latch_2a7b4e3e_1 (.Q(nor_latch_2a7b4e3e_1_q), .R(or_2_out), .S(or_1_out));
  NOR_LATCH_2a7b4e3e nor_latch_2a7b4e3e_2 (.Q(nor_latch_2a7b4e3e_2_q), .R(or_4_out), .S(or_3_out));
  NOR_LATCH_2a7b4e3e nor_latch_2a7b4e3e_3 (.Q(nor_latch_2a7b4e3e_3_q), .R(or_6_out), .S(or_5_out));
  NOR_LATCH_2a7b4e3e nor_latch_2a7b4e3e_4 (.Q(nor_latch_2a7b4e3e_4_q), .R(or_8_out), .S(or_7_out));
  and and_5 (and_5_out, nor_latch_2a7b4e3e_4_q, POS_4_90082566);
  and and_6 (and_6_out, nor_latch_2a7b4e3e_3_q, POS_3_0e2c95fa);
  and and_7 (and_7_out, nor_latch_2a7b4e3e_2_q, POS_2_66b3fa52);
  and and_8 (and_8_out, nor_latch_2a7b4e3e_1_q, POS_1_63d6ef2b);
  or or_9 (AT_STOP_46b7d8da, and_8_out, and_7_out, and_6_out, and_5_out);
  or or_10 (or_10_out, nor_latch_2a7b4e3e_4_q, nor_latch_2a7b4e3e_3_q);
  or or_11 (or_11_out, nor_latch_2a7b4e3e_4_q, nor_latch_2a7b4e3e_3_q, nor_latch_2a7b4e3e_2_q);
  or or_12 (or_12_out, nor_latch_2a7b4e3e_3_q, nor_latch_2a7b4e3e_2_q, nor_latch_2a7b4e3e_1_q);
  or or_13 (or_13_out, nor_latch_2a7b4e3e_2_q, nor_latch_2a7b4e3e_1_q);
  and and_9 (and_9_out, nor_latch_2a7b4e3e_4_q, POS_3_0e2c95fa);
  and and_10 (and_10_out, or_10_out, POS_2_66b3fa52);
  and and_11 (and_11_out, or_11_out, POS_1_63d6ef2b);
  and and_12 (and_12_out, or_12_out, POS_4_90082566);
  and and_13 (and_13_out, or_13_out, POS_3_0e2c95fa);
  and and_14 (and_14_out, nor_latch_2a7b4e3e_1_q, POS_2_66b3fa52);
  or or_14 (CALL_ACTIVE_715e6a8a, nor_latch_2a7b4e3e_1_q, nor_latch_2a7b4e3e_2_q, nor_latch_2a7b4e3e_3_q, nor_latch_2a7b4e3e_4_q);
  or or_15 (CALL_ABOVE_715101cc, and_9_out, and_10_out, and_11_out);
  or or_16 (CALL_BELOW_fc8ecee0, and_12_out, and_13_out, and_14_out);

  // Notes on the sheet:
  //   1
  //   2
  //   3
  //   4
  //   Position 4321
  //   Calls Latched
  //   P4321
  //   3
  //   2
  //   1
  //   4
  //   3
  //   2
endmodule

module ONE_SHOT_5a75b42e (
  input  TRIG,
  output OUTPUT
);

  wire clock_1_out, counter_1_carry, not_1_out;
  wire [3:0] counter_1_q, undriven;

  Clock clock_1 (.out(clock_1_out));
  Counter #(.max('hf), .width(4)) counter_1 (
    .load(1'b1), .D(undriven), .count(1'b1), .Q(counter_1_q), .carry(counter_1_carry), .clk(clock_1_out),
    .clr(not_1_out));  // open: up
  not not_1 (not_1_out, OUTPUT);
  NOR_LATCH_2a7b4e3e nor_latch_2a7b4e3e_1 (.Q(OUTPUT), .R(counter_1_carry), .S(TRIG));

  // Notes on the sheet:
  //   ONE-SHOT TIMER
  //   LOAD & COUNT 
  //   DON'T NEED PULLUPS
  //   POSITIVE PULSE
  //   DATA
  //   LOAD
  //   COUNT
  //   CLK
  //   0: Q=d, 1=COUNT
  //   Q
  //   CARRY
endmodule

module DOOR_SIM_7d0fcb8b (
  input  CMD_OPEN_629398b5,
  output DOOR_STATUS_af08e2fd
);

  wire and_1_out, clock_1_out, nor_latch_2a7b4e3e_1_q, nor_latch_2a7b4e3e_2_q, not_1_out, not_2_out,
       shift_register_1_p6, shift_register_1_p7, shift_register_1_p8;

  not not_1 (not_1_out, nor_latch_2a7b4e3e_2_q);
  and and_1 (and_1_out, not_1_out, CMD_OPEN_629398b5);
  NOR_LATCH_2a7b4e3e nor_latch_2a7b4e3e_1 (.Q(nor_latch_2a7b4e3e_1_q), .R(shift_register_1_p6), .S(and_1_out));
  NOR_LATCH_2a7b4e3e nor_latch_2a7b4e3e_2 (
    .Q(nor_latch_2a7b4e3e_2_q), .R(shift_register_1_p8), .S(shift_register_1_p6));
  Clock clock_1 (.out(clock_1_out));
  // Shift_Register #(.length(5)) shift_register_1: pin names not known; wires that end beside it: 1'b1, nor_latch_2a7b4e3e_1_q, clock_1_out, 1'b0, 1'b0, shift_register_1_p6, shift_register_1_p7, shift_register_1_p8
  NOR_LATCH_2a7b4e3e nor_latch_2a7b4e3e_3 (.Q(DOOR_STATUS_af08e2fd), .R(shift_register_1_p8), .S(shift_register_1_p7));
  LED OPEN (.in(DOOR_STATUS_af08e2fd));
  not not_2 (not_2_out, DOOR_STATUS_af08e2fd);
  LED CLOSED (.in(not_2_out));

  // Notes on the sheet:
  //   SHIFT
  //   CLK
  //   LD
  //   CLR
  //   OPENED
  //   CLOSED
endmodule

module POSITION_SIM_da48c610 (
  input  MOTOR_UP_48e201b7,
  input  MOTOR_DN_f43bb3b6,
  output SIM_POS_1_ba810d2c,
  output SIM_POS_2_53fc652d,
  output SIM_POS_3_678ab255,
  output SIM_POS_4_123cdcbe
);

  wire and_1_out, and_2_out, and_3_out, and_4_out, and_5_out, clock_1_out, counter_1_carry, not_1_out,
       not_2_out, not_3_out, not_4_out, or_1_out;
  wire [1:0] counter_1_q;

  and and_1 (and_1_out, MOTOR_UP_48e201b7, not_3_out);
  and and_2 (and_2_out, MOTOR_DN_f43bb3b6, not_4_out);
  not not_1 (not_1_out, and_1_out);
  not not_2 (not_2_out, and_2_out);
  not not_3 (not_3_out, SIM_POS_4_123cdcbe);
  not not_4 (not_4_out, SIM_POS_1_ba810d2c);
  and and_3 (and_3_out, not_1_out, and_2_out);
  and and_4 (and_4_out, and_1_out, not_2_out);
  and and_5 (and_5_out, not_1_out, and_2_out);
  or or_1 (or_1_out, and_4_out, and_5_out);
  Counter #(.max('h3), .width(2)) counter_1 (
    .load(and_3_out), .D(2'b00), .count(or_1_out), .Q(counter_1_q), .carry(counter_1_carry),
    .clk(clock_1_out), .clr(1'b0));  // open: up
  Clock clock_1 (.out(clock_1_out));
  Decoder #(.enable("false"), .select(2)) decoder_1 (
    .out0(SIM_POS_1_ba810d2c), .out1(SIM_POS_2_53fc652d), .out2(SIM_POS_3_678ab255),
    .out3(SIM_POS_4_123cdcbe), .sel(counter_1_q));

  // Notes on the sheet:
  //   UP EN
  //   DOWN EN
  //   CAR POSITION SIMULATOR
  //   LD
  //   CLK
  //   Q
  //   CY
  //   CLR
  //   UP
  //   DN
  //   FLIP-FLOP
  //   CNT
  //   LD
  //   0
  //   1
  //   1
  //   1
endmodule

module DIRECTION_DECODE_e6330b5d (
  input  UP_CALL_39970cbc,
  input  DOWN_CALL_4aac5db2,
  output DIRECTION
);

  wire and_1_out, and_2_out, and_3_out, not_1_out, not_2_out, not_3_out;

  not not_1 (not_1_out, DIRECTION);
  not not_2 (not_2_out, DOWN_CALL_4aac5db2);
  not not_3 (not_3_out, DOWN_CALL_4aac5db2);
  and and_1 (and_1_out, not_1_out, UP_CALL_39970cbc, not_2_out);
  and and_2 (and_2_out, DIRECTION, UP_CALL_39970cbc, not_3_out);
  and and_3 (and_3_out, DIRECTION, UP_CALL_39970cbc, DOWN_CALL_4aac5db2);
  or or_1 (DIRECTION, and_1_out, and_2_out, and_3_out);

  // Notes on the sheet:
  //   1=UP
endmodule
